// Logisim project lab3.circ as structural Verilog: 1 circuit, main circuit main
module main (
  input  in_1,
  input  in_2,
  output Out_S,
  output Out_Q
);

  and and_1 (Out_S, in_1, in_2);
  xor xor_1 (Out_Q, in_1, ~in_2);  // XOR_Gate
endmodule
