// Logisim project lab4ec.circ as structural Verilog: 2 circuits, main circuit main
module main (
  input  Subtract,
  input  [3:0] in_2,
  input  [3:0] in_3,
  output [3:0] Output,
  output Cout
);

  wire n1_bit_adder_1_cout, n1_bit_adder_2_cout, n1_bit_adder_3_cout;
  wire [3:0] xor_1_out;

  xor xor_1 (xor_1_out[0], Subtract, in_3[0]);
  xor xor_2 (xor_1_out[1], Subtract, in_3[1]);
  xor xor_3 (xor_1_out[2], Subtract, in_3[2]);
  xor xor_4 (xor_1_out[3], Subtract, in_3[3]);
  _1_bit_adder u_1_bit_adder_1 (
    .A(in_2[0]), .B(xor_1_out[0]), .Cin(Subtract), .Sum(Output[0]), .Cout(n1_bit_adder_1_cout));
  _1_bit_adder u_1_bit_adder_2 (
    .A(in_2[1]), .B(xor_1_out[1]), .Cin(n1_bit_adder_1_cout), .Sum(Output[1]), .Cout(n1_bit_adder_2_cout));
  _1_bit_adder u_1_bit_adder_3 (
    .A(in_2[2]), .B(xor_1_out[2]), .Cin(n1_bit_adder_2_cout), .Sum(Output[2]), .Cout(n1_bit_adder_3_cout));
  _1_bit_adder u_1_bit_adder_4 (.A(in_2[3]), .B(xor_1_out[3]), .Cin(n1_bit_adder_3_cout), .Sum(Output[3]), .Cout(Cout));
endmodule

module _1_bit_adder (
  input  A,
  input  B,
  input  Cin,
  output Sum,
  output Cout
);

  wire All_3_out, Any_2_out, Only_1_out;

  and All_3 (All_3_out, A, B, Cin);
  ExactlyOne Only_1 (.out(Only_1_out), .in0(A), .in1(B), .in3(Cin));
  ExactlyOne Any_2 (.out(Any_2_out), .in0(A), .in1(B), .in2(Cin));
  or or_1 (Sum, All_3_out, Only_1_out);
  or or_2 (Cout, All_3_out, Any_2_out);
endmodule
