// Logisim project lab6alu.circ as structural Verilog: 4 circuits, main circuit main
module main (
  input  [7:0] A,
  input  [7:0] B,
  input  [1:0] OP,
  input  Write,
  output [7:0] Q,
  output V,
  output Z,
  output N
);

  wire and_2_out, and_3_out, not_2_out, or_2_out, or_3_out;
  wire [7:0] _8bitadd_out_3, and_1_out, not_1_out, or_1_out;

  assign not_1_out = ~A;  // NOT_Gate not_1, 8 bits wide
  assign and_1_out = A & B;  // AND_Gate and_1, 8 bits wide
  assign or_1_out = A | B;  // OR_Gate or_1, 8 bits wide
  _8bitadder _8bitadd (.A(A), .B(B), .out_3(_8bitadd_out_3));
  and and_2 (and_2_out, ~A[7], ~B[7], Q[7]);  // AND_Gate
  and and_3 (and_3_out, A[7], B[7], ~Q[7]);  // AND_Gate
  or or_2 (or_2_out, and_2_out, and_3_out);
  D_flip_flop d_flip_flop_1 (.In(or_2_out), .Write(Write), .out_3(V));  // open: out_4
  D_flip_flop d_flip_flop_2 (.In(not_2_out), .Write(Write), .out_3(Z));  // open: out_4
  D_flip_flop d_flip_flop_3 (.In(Q[7]), .Write(Write), .out_3(N));  // open: out_4
  Multiplexer #(.select(2), .width(8)) multiplexer_1 (
    .in0(not_1_out), .in1(and_1_out), .in2(or_1_out), .in3(_8bitadd_out_3), .out(Q), .sel(OP));  // open: en
  or or_3 (or_3_out, Q[0], Q[1], Q[2], Q[3], Q[4], Q[5], Q[6], Q[7]);
  not not_2 (not_2_out, or_3_out);
endmodule

module adder (
  input  A,
  input  B,
  input  Cin,
  output Sum,
  output Cout
);

  wire All_3_out, Any_2_out, Only_1_out;

  and All_3 (All_3_out, A, B, Cin);
  ExactlyOne Only_1 (.out(Only_1_out), .in0(A), .in1(B), .in3(Cin));
  ExactlyOne Any_2 (.out(Any_2_out), .in0(A), .in1(B), .in2(Cin));
  or or_1 (Sum, All_3_out, Only_1_out);
  or or_2 (Cout, All_3_out, Any_2_out);
endmodule

module _8bitadder (
  input  [7:0] A,
  input  [7:0] B,
  output [7:0] out_3
);

  wire adder_1_cout, adder_2_cout, adder_3_cout, adder_4_cout, adder_5_cout, adder_6_cout, adder_7_cout,
       pull_resistor_1_node;

  Pull_Resistor pull_resistor_1 (.node(pull_resistor_1_node));
  adder adder_1 (.A(A[0]), .B(B[0]), .Cin(pull_resistor_1_node), .Sum(out_3[0]), .Cout(adder_1_cout));
  adder adder_2 (.A(A[1]), .B(B[1]), .Cin(adder_1_cout), .Sum(out_3[1]), .Cout(adder_2_cout));
  adder adder_3 (.A(A[2]), .B(B[2]), .Cin(adder_2_cout), .Sum(out_3[2]), .Cout(adder_3_cout));
  adder adder_4 (.A(A[3]), .B(B[3]), .Cin(adder_3_cout), .Sum(out_3[3]), .Cout(adder_4_cout));
  adder adder_5 (.A(A[4]), .B(B[4]), .Cin(adder_4_cout), .Sum(out_3[4]), .Cout(adder_5_cout));
  adder adder_6 (.A(A[5]), .B(B[5]), .Cin(adder_5_cout), .Sum(out_3[5]), .Cout(adder_6_cout));
  adder adder_7 (.A(A[6]), .B(B[6]), .Cin(adder_6_cout), .Sum(out_3[6]), .Cout(adder_7_cout));
  adder adder_8 (.A(A[7]), .B(B[7]), .Cin(adder_7_cout), .Sum(out_3[7]));  // open: Cout
endmodule

module D_flip_flop (
  input  In,
  input  Write,
  output out_3,
  output out_4
);

  wire and_1_out, and_2_out, not_1_out, not_2_out;

  and and_1 (and_1_out, In, Write);
  and and_2 (and_2_out, Write, ~In);  // AND_Gate
  not not_1 (not_1_out, and_1_out);
  not not_2 (not_2_out, and_2_out);
  nand nand_1 (out_3, not_1_out, out_4);
  nand nand_2 (out_4, out_3, not_2_out);
endmodule
